// Logisim project prime_counter.circ as structural Verilog: 1 circuit, main circuit main
module main (
);

  wire and_1_out, and_2_out, and_3_out, and_4_out, and_5_out, and_6_out, and_7_out, and_8_out, clock_1_out,
       d_ff_1_qn, d_ff_2_qn, d_ff_3_qn, d_ff_4_qn, d_ff_5_qn, d_ff_6_qn, d_ff_7_qn, d_ff_8_qn, or_1_out,
       or_2_out, or_3_out, or_4_out, or_5_out, or_6_out, or_7_out, or_8_out, or_9_out, or_10_out, or_11_out,
       or_12_out, or_13_out, or_14_out, or_15_out, or_16_out, or_17_out, or_18_out, or_19_out, or_20_out,
       or_21_out, or_22_out, or_23_out, or_24_out, or_25_out, or_26_out, or_27_out, or_28_out, or_29_out,
       or_30_out, or_31_out, or_32_out, or_33_out, or_34_out, or_35_out, or_36_out, or_37_out, or_38_out,
       or_39_out, or_40_out, or_41_out, or_42_out, or_43_out, or_44_out, or_45_out, or_46_out, or_47_out,
       or_48_out, or_49_out, or_50_out, or_51_out, or_52_out, or_53_out, or_54_out, or_55_out;
  wire [7:0] d_ff_8_q;

  D_Flip_Flop d_ff_1 (.D(and_1_out), .clk(clock_1_out), .Q(d_ff_8_q[7]), .Qn(d_ff_1_qn));  // open: preset, reset
  D_Flip_Flop d_ff_2 (.D(and_2_out), .clk(clock_1_out), .Q(d_ff_8_q[6]), .Qn(d_ff_2_qn));  // open: preset, reset
  D_Flip_Flop d_ff_3 (.D(and_3_out), .clk(clock_1_out), .Q(d_ff_8_q[5]), .Qn(d_ff_3_qn));  // open: preset, reset
  D_Flip_Flop d_ff_4 (.D(and_4_out), .clk(clock_1_out), .Q(d_ff_8_q[4]), .Qn(d_ff_4_qn));  // open: preset, reset
  D_Flip_Flop d_ff_5 (.D(and_5_out), .clk(clock_1_out), .Q(d_ff_8_q[3]), .Qn(d_ff_5_qn));  // open: preset, reset
  D_Flip_Flop d_ff_6 (.D(and_6_out), .clk(clock_1_out), .Q(d_ff_8_q[2]), .Qn(d_ff_6_qn));  // open: preset, reset
  D_Flip_Flop d_ff_7 (.D(and_7_out), .clk(clock_1_out), .Q(d_ff_8_q[1]), .Qn(d_ff_7_qn));  // open: preset, reset
  D_Flip_Flop d_ff_8 (.D(and_8_out), .clk(clock_1_out), .Q(d_ff_8_q[0]), .Qn(d_ff_8_qn));  // open: preset, reset
  Clock clock_1 (.out(clock_1_out));
  and and_1 (and_1_out, or_1_out, or_2_out, or_3_out, or_4_out);
  and and_2 (and_2_out, or_5_out, or_6_out, or_7_out, or_8_out, or_9_out);
  and and_3 (and_3_out, or_10_out, or_11_out, or_12_out, or_13_out, or_14_out);
  and and_4 (and_4_out, or_15_out, or_16_out, or_17_out, or_18_out, or_19_out, or_20_out, or_21_out, or_22_out);
  and and_5 (and_5_out, or_23_out, or_24_out, or_25_out, or_26_out, or_27_out, or_28_out, or_29_out, or_30_out, or_31_out, or_32_out, or_33_out);
  and and_6 (and_6_out, d_ff_8_q[0], or_34_out, or_35_out, or_36_out, or_37_out, or_38_out, or_39_out, or_40_out, or_41_out, or_42_out);
  and and_7 (and_7_out, or_43_out, or_44_out, or_45_out, or_46_out, or_47_out, or_48_out, or_49_out, or_50_out, or_51_out, or_52_out, or_53_out);
  and and_8 (and_8_out, or_54_out, or_55_out);
  or or_1 (or_1_out, d_ff_8_q[7], d_ff_8_q[6]);
  or or_2 (or_2_out, d_ff_8_q[7], d_ff_8_q[4]);
  or or_3 (or_3_out, d_ff_8_q[7], d_ff_8_q[2]);
  or or_4 (or_4_out, d_ff_1_qn, d_ff_2_qn, d_ff_3_qn, d_ff_4_qn, d_ff_7_qn);
  or or_5 (or_5_out, d_ff_8_q[6], d_ff_8_q[5]);
  or or_6 (or_6_out, d_ff_8_q[6], d_ff_8_q[4]);
  or or_7 (or_7_out, d_ff_8_q[6], d_ff_8_q[3]);
  or or_8 (or_8_out, d_ff_8_q[6], d_ff_8_q[2]);
  or or_9 (or_9_out, d_ff_2_qn, d_ff_3_qn, d_ff_4_qn, d_ff_7_qn);
  or or_10 (or_10_out, d_ff_8_q[5], d_ff_8_q[4]);
  or or_11 (or_11_out, d_ff_8_q[5], d_ff_8_q[3]);
  or or_12 (or_12_out, d_ff_8_q[7], d_ff_8_q[6], d_ff_8_q[1], d_ff_5_qn, d_ff_6_qn);
  or or_13 (or_13_out, d_ff_2_qn, d_ff_3_qn, d_ff_4_qn, d_ff_7_qn);
  or or_14 (or_14_out, d_ff_3_qn, d_ff_4_qn, d_ff_5_qn, d_ff_6_qn);
  or or_15 (or_15_out, d_ff_8_q[7], d_ff_8_q[4], d_ff_8_q[3]);
  or or_16 (or_16_out, d_ff_8_q[6], d_ff_8_q[4], d_ff_8_q[3]);
  or or_17 (or_17_out, d_ff_8_q[4], d_ff_8_q[2], d_ff_3_qn);
  or or_18 (or_18_out, d_ff_8_q[2], d_ff_8_q[1], d_ff_5_qn);
  or or_19 (or_19_out, d_ff_1_qn, d_ff_4_qn, d_ff_5_qn);
  or or_20 (or_20_out, d_ff_8_q[4], d_ff_8_q[1], d_ff_1_qn, d_ff_2_qn);
  or or_21 (or_21_out, d_ff_8_q[7], d_ff_8_q[6], d_ff_8_q[5], d_ff_5_qn, d_ff_7_qn);
  or or_22 (or_22_out, d_ff_3_qn, d_ff_4_qn, d_ff_5_qn, d_ff_6_qn);
  or or_23 (or_23_out, d_ff_8_q[7], d_ff_8_q[6], d_ff_8_q[3], d_ff_8_q[2]);
  or or_24 (or_24_out, d_ff_8_q[7], d_ff_8_q[4], d_ff_8_q[3], d_ff_8_q[2]);
  or or_25 (or_25_out, d_ff_8_q[5], d_ff_8_q[4], d_ff_8_q[1], d_ff_6_qn);
  or or_26 (or_26_out, d_ff_1_qn, d_ff_5_qn, d_ff_7_qn);
  or or_27 (or_27_out, d_ff_2_qn, d_ff_4_qn, d_ff_5_qn);
  or or_28 (or_28_out, d_ff_3_qn, d_ff_5_qn, d_ff_6_qn);
  or or_29 (or_29_out, d_ff_5_qn, d_ff_6_qn, d_ff_7_qn);
  or or_30 (or_30_out, d_ff_8_q[5], d_ff_8_q[4], d_ff_1_qn, d_ff_2_qn);
  or or_31 (or_31_out, d_ff_8_q[5], d_ff_8_q[1], d_ff_1_qn, d_ff_6_qn);
  or or_32 (or_32_out, d_ff_8_q[3], d_ff_8_q[2], d_ff_3_qn, d_ff_7_qn);
  or or_33 (or_33_out, d_ff_8_q[7], d_ff_8_q[4], d_ff_8_q[1], d_ff_2_qn, d_ff_3_qn);
  or or_34 (or_34_out, d_ff_8_q[6], d_ff_8_q[2], d_ff_8_q[1]);
  or or_35 (or_35_out, d_ff_8_q[7], d_ff_8_q[6], d_ff_8_q[1], d_ff_3_qn);
  or or_36 (or_36_out, d_ff_1_qn, d_ff_4_qn, d_ff_5_qn);
  or or_37 (or_37_out, d_ff_2_qn, d_ff_6_qn, d_ff_7_qn);
  or or_38 (or_38_out, d_ff_8_q[7], d_ff_8_q[5], d_ff_2_qn, d_ff_4_qn);
  or or_39 (or_39_out, d_ff_8_q[5], d_ff_8_q[4], d_ff_6_qn, d_ff_7_qn);
  or or_40 (or_40_out, d_ff_8_q[4], d_ff_8_q[1], d_ff_5_qn, d_ff_6_qn);
  or or_41 (or_41_out, d_ff_8_q[5], d_ff_8_q[4], d_ff_8_q[3], d_ff_1_qn, d_ff_7_qn);
  or or_42 (or_42_out, d_ff_8_q[3], d_ff_8_q[1], d_ff_1_qn, d_ff_2_qn, d_ff_3_qn);
  or or_43 (or_43_out, d_ff_8_q[7], d_ff_8_q[5], d_ff_2_qn, d_ff_4_qn);
  or or_44 (or_44_out, d_ff_8_q[4], d_ff_8_q[3], d_ff_8_q[2], d_ff_8_q[1], d_ff_8_qn);
  or or_45 (or_45_out, d_ff_8_q[6], d_ff_3_qn, d_ff_4_qn, d_ff_7_qn);
  or or_46 (or_46_out, d_ff_8_q[6], d_ff_3_qn, d_ff_6_qn, d_ff_7_qn);
  or or_47 (or_47_out, d_ff_8_q[6], d_ff_4_qn, d_ff_6_qn, d_ff_7_qn);
  or or_48 (or_48_out, d_ff_8_q[7], d_ff_8_q[6], d_ff_8_q[4], d_ff_3_qn, d_ff_6_qn);
  or or_49 (or_49_out, d_ff_8_q[7], d_ff_8_q[4], d_ff_8_q[1], d_ff_5_qn, d_ff_6_qn);
  or or_50 (or_50_out, d_ff_8_q[7], d_ff_8_q[5], d_ff_8_q[3], d_ff_2_qn, d_ff_6_qn);
  or or_51 (or_51_out, d_ff_1_qn, d_ff_2_qn, d_ff_3_qn, d_ff_6_qn);
  or or_52 (or_52_out, d_ff_8_q[4], d_ff_8_q[2], d_ff_2_qn, d_ff_3_qn, d_ff_7_qn);
  or or_53 (or_53_out, d_ff_8_q[6], d_ff_8_q[5], d_ff_8_q[4], d_ff_8_q[2], d_ff_7_qn, d_ff_8_qn);
  or or_54 (or_54_out, d_ff_8_q[6], d_ff_8_q[4], d_ff_8_q[3], d_ff_8_q[2], d_ff_8_q[1]);
  or or_55 (or_55_out, d_ff_1_qn, d_ff_2_qn, d_ff_3_qn, d_ff_4_qn, d_ff_7_qn);
  // Probe on d_ff_8_q
endmodule
